# Fritzing sketch Snap_Shoot_1 (saved by Fritzing 0.9.3b)
breadboards: 1

parts:
  Raspberry_Pi_1 = Raspberry Pi 3 [part_number=RPI-3-V1.2]
  S2 = Pushbutton [package="[SMD]"]
  S3 = Pushbutton [package="[SMD]"]

nets:
  N1: Raspberry_Pi_1.GIPO17, Raspberry_Pi_1.GND, S2.Pin_3, S2.Pin_4
  N2: Raspberry_Pi_1.GIPO27, S3.Pin_1, S3.Pin_2
